// Logisim project cpu.circ as structural Verilog: 1 circuit, main circuit cpu
module cpu (
  input  clk,
  input  [31:0] Instruction,
  input  [31:0] MemReadData,
  output [31:0] MemAddress,
  output [31:0] ProgramCounter,
  output [31:0] ra,
  output [31:0] sp,
  output [31:0] t0,
  output [31:0] t1,
  output [31:0] t2,
  output [31:0] s0,
  output [31:0] s1,
  output [31:0] a0,
  output [3:0] MemWriteMask,
  output [31:0] MemWriteData
);

  wire Bsel, lb, MemWEn, RegWEn;
  wire [1:0] WBSel;
  wire [2:0] ImmSel;
  wire [3:0] ALUSel;
  wire [31:0] adder_1_out, bit_extender_1_out, imm_gen_1_immediate, multiplexer_1_out, r1, r2, ReadData2,
       WriteData;

  Register #(.width(32)) PC (.D(adder_1_out), .clk(clk), .Q(ProgramCounter));  // open: en, clr
  Adder #(.width(32)) adder_1 (.a(ProgramCounter), .b(32'h4), .out(adder_1_out));  // open: cin, cout
  control_logic control_logic_1 (
    .Instruction(Instruction), .RegWEn(RegWEn), .ImmSel(ImmSel), .BSel(Bsel), .ALUSel(ALUSel),
    .MemWEn(MemWEn), .WBSel(WBSel), .out_13(lb));  // open: BrEq, BrLt, out_15, out_16, out_17, PCSel, BrUn, ASel, out_14
  regfile regfile_1 (
    .ReadIndex1(Instruction[19:15]), .ReadIndex2(Instruction[24:20]), .WriteIndex(Instruction[11:7]),
    .WriteData(WriteData), .RegWEn(RegWEn), .clk(clk), .ra(ra), .sp(sp), .t0(t0), .t1(t1), .t2(t2), .s0(s0),
    .s1(s1), .a0(a0), .ReadData1(r1), .ReadData2(r2));
  imm_gen imm_gen_1 (.Instruction(Instruction), .ImmSel(ImmSel), .Immediate(imm_gen_1_immediate));
  Multiplexer #(.width(32)) multiplexer_1 (.in0(r2), .in1(imm_gen_1_immediate), .out(multiplexer_1_out), .sel(Bsel));
  alu alu_1 (.A(r1), .B(multiplexer_1_out), .ALUSel(ALUSel), .ALUResult(MemAddress));
  // branch_comp branch_comp_1: pin names not known
  Multiplexer #(.select(2), .width(32)) multiplexer_2 (
    .in0(ReadData2), .in1(MemAddress), .out(WriteData), .sel(WBSel));  // open: in2, in3
  Multiplexer #(.width(4)) multiplexer_3 (.in0(4'b0000), .in1(4'b0000), .out(MemWriteMask), .sel(MemWEn));
  // partial_store partial_store_1: pin names not known
  // partial_load partial_load_1: pin names not known
  assign bit_extender_1_out = {{24{MemReadData[7]}}, MemReadData[7:0]};  // Bit_Extender bit_extender_1
  Multiplexer #(.width(32)) multiplexer_4 (.in0({32{1'b1}}), .in1(bit_extender_1_out), .out(ReadData2), .sel(lb));

  // Other names for the same wires on the sheet: opcode[6:0] = Instruction[6:0]; WriteReg[4:0] = Instruction[11:7];
  //   func3[2:0] = Instruction[14:12]; ReadReg1[4:0] = Instruction[19:15]; ReadReg2[4:0] = Instruction[24:20];
  //   func7[6:0] = Instruction[31:25]

  // Notes on the sheet:
  //   Instruction Decode
  //   To IMEM
  //   IMEM (do **NOT** move this)
  //   From IMEM
  //   Inputs/Outputs for testing. Do **NOT** move these.
  //   It is OK to move the PC, RegFile, ALU, MEM, Branch Comp, Imm Gen, Partial Load, Partial Store and Control Logic to wherever is most convenient for you when constructing your CPU, and to delete this text
  //   We want to select MemAddress for lb
  //   To DMEM
  //   DMEM (do **NOT** move this)
  //   From DMEM
endmodule
